// Digital circuit 744078.dig as structural Verilog
module _744078 (
  input  H,
  input  G,
  input  F,
  input  E,
  input  D,
  input  C,
  input  B,
  input  A,
  input  VCC,
  input  GND,
  output X,
  output Y
);

  nor nor_1 (X, H, G, F, E, D, C, B, A);
  PowerSupply powersupply_1 (.VDD(VCC), .GND(GND));
  not not_1 (Y, X);

  // Notes on the sheet:
  //   H: pin 12
  //   G: pin 11
  //   F: pin 10
  //   E: pin 9
  //   D: pin 5
  //   C: pin 4
  //   B: pin 3
  //   A: pin 2
  //   X: pin 13
  //   Y: pin 1
  //   VCC: pin 14
  //   GND: pin 7
endmodule
