// Digital circuit CPU.dig as structural Verilog
module CPU (
  input  in_1,
  input  in_2,
  input  in_3,
  input  in_4,
  input  clk,
  input  [1:0] in_7,
  input  in_8,
  input  [7:0] in_9,
  output [7:0] out_5
);

  wire and_1_out, and_2_out, and_3_out, and_4_out, and_5_out, and_6_out, and_7_out, and_8_out,
       decoder_1_out_0, decoder_1_out_1, decoder_1_out_2, demultiplexer_1_out_0, demultiplexer_1_out_1,
       demultiplexer_1_out_2, demultiplexer_1_out_3, not_1_out, not_2_out, or_1_out;
  wire [1:0] counter_1_out;
  wire [7:0] R1_q, R2_q, R3_q, R4_q;

  Counter #(.Bits(2)) counter_1 (.en(1'b1), .C(clk), .clr(1'b0), .out(counter_1_out));  // open: ovf
  Demultiplexer #(.Selector_Bits(2)) demultiplexer_1 (
    .sel(in_7), .in(in_8), .out_0(demultiplexer_1_out_0), .out_1(demultiplexer_1_out_1),
    .out_2(demultiplexer_1_out_2), .out_3(demultiplexer_1_out_3));
  Decoder #(.Selector_Bits(2)) decoder_1 (
    .sel(counter_1_out), .out_0(decoder_1_out_0), .out_1(decoder_1_out_1), .out_2(decoder_1_out_2));  // open: out_3
  not not_1 (not_1_out, decoder_1_out_2);
  and and_1 (and_1_out, demultiplexer_1_out_0, not_1_out);
  and and_2 (and_2_out, demultiplexer_1_out_1, not_1_out);
  and and_3 (and_3_out, demultiplexer_1_out_2, not_1_out);
  and and_4 (and_4_out, demultiplexer_1_out_3, not_1_out);
  assign out_5 = decoder_1_out_0 ? in_9 : 8'bz;  // Driver driver_1
  or or_1 (or_1_out, decoder_1_out_1, decoder_1_out_2);
  not not_2 (not_2_out, clk);
  Register #(.Bits(8)) R1 (.D(out_5), .C(not_2_out), .en(and_1_out), .Q(R1_q));
  Register #(.Bits(8)) R2 (.D(out_5), .C(not_2_out), .en(and_2_out), .Q(R2_q));
  Register #(.Bits(8)) R3 (.D(out_5), .C(not_2_out), .en(and_3_out), .Q(R3_q));
  Register #(.Bits(8)) R4 (.D(out_5), .C(not_2_out), .en(and_4_out), .Q(R4_q));
  and and_5 (and_5_out, in_1, or_1_out);
  assign out_5 = and_5_out ? R1_q : 8'bz;  // Driver driver_2
  and and_6 (and_6_out, in_2, or_1_out);
  assign out_5 = and_6_out ? R2_q : 8'bz;  // Driver driver_3
  and and_7 (and_7_out, in_3, or_1_out);
  assign out_5 = and_7_out ? R3_q : 8'bz;  // Driver driver_4
  and and_8 (and_8_out, in_4, or_1_out);
  assign out_5 = and_8_out ? R4_q : 8'bz;  // Driver driver_5

  // Notes on the sheet:
  //   clk: Hz: 4
endmodule
