// Digital circuit rFlags.dig as structural Verilog
module rFlags (
  input  clk
);

  wire _7404_1_pin2, _7404_1_pin4, _7404_1_pin12, _7432_1_pin3, _74573_1_pin12, _74573_1_pin13,
       _74573_1_pin14, _74573_1_pin15, _74573_1_pin16, _74573_1_pin17, _74573_1_pin18, _74573_1_pin19,
       _744078_1_x, dipswitch_1_out, dipswitch_2_out, dipswitch_3_out, dipswitch_4_out, dipswitch_5_out,
       dipswitch_6_out, dipswitch_7_out, dipswitch_8_out;

  DipSwitch dipswitch_1 (.out(dipswitch_1_out));
  DipSwitch dipswitch_2 (.out(dipswitch_2_out));
  DipSwitch dipswitch_3 (.out(dipswitch_3_out));
  DipSwitch dipswitch_4 (.out(dipswitch_4_out));
  DipSwitch dipswitch_5 (.out(dipswitch_5_out));
  DipSwitch dipswitch_6 (.out(dipswitch_6_out));
  DipSwitch dipswitch_7 (.out(dipswitch_7_out));
  DipSwitch dipswitch_8 (.out(dipswitch_8_out));
  _744078 _744078_1 (
    .H(dipswitch_8_out), .G(dipswitch_7_out), .F(dipswitch_6_out), .E(dipswitch_5_out), .D(dipswitch_4_out),
    .C(dipswitch_3_out), .B(dipswitch_2_out), .A(dipswitch_1_out), .X(_744078_1_x), .VCC(1'b1), .GND(1'b0));  // open: Y
  _7432 _7432_1 (
    .pin1(_744078_1_x), .pin2(dipswitch_4_out), .pin3(_7432_1_pin3), .pin4(1'b0), .pin5(1'b0), .pin7(1'b0),
    .pin9(1'b0), .pin10(1'b0), .pin12(1'b0), .pin13(1'b0), .pin14(1'b1));  // open: pin6, pin8, pin11
  _7404 _7404_1 (
    .pin1(_7432_1_pin3), .pin2(_7404_1_pin2), .pin3(dipswitch_4_out), .pin4(_7404_1_pin4), .pin5(1'b0),
    .pin7(1'b0), .pin9(1'b0), .pin11(1'b0), .pin12(_7404_1_pin12), .pin13(_744078_1_x), .pin14(1'b1));  // open: pin6, pin8, pin10
  _74573 _74573_1 (
    .pin1(1'b0), .pin2(_744078_1_x), .pin3(_7404_1_pin12), .pin4(_7404_1_pin2), .pin5(_7404_1_pin4),
    .pin6(dipswitch_4_out), .pin7(_7432_1_pin3), .pin8(1'b0), .pin9(1'b0), .pin10(1'b0), .pin11(clk),
    .pin12(_74573_1_pin12), .pin13(_74573_1_pin13), .pin14(_74573_1_pin14), .pin15(_74573_1_pin15),
    .pin16(_74573_1_pin16), .pin17(_74573_1_pin17), .pin18(_74573_1_pin18), .pin19(_74573_1_pin19),
    .pin20(1'b1));
  LED led_1 (.in(_74573_1_pin19));
  LED led_2 (.in(_74573_1_pin18));
  LED led_3 (.in(_74573_1_pin17));
  LED led_4 (.in(_74573_1_pin16));
  LED led_5 (.in(_74573_1_pin15));
  LED led_6 (.in(_74573_1_pin14));
  LED led_7 (.in(_74573_1_pin13));
  LED led_8 (.in(_74573_1_pin12));

  // Notes on the sheet:
  //   clk: Hz: 10
  //   eq
  //   neq
  //   jg
  //   jge
  //   jle
  //   jl
endmodule
